# Fritzing sketch NesClassicAdvantage (saved by Fritzing 0.9.3b)
breadboards: 1

parts:
  U1 = atmega328 [package=dip]
  S1 = Pushbutton [package="[THT]"]
  S2 = Pushbutton [package="[THT]"]
  S3 = Pushbutton [package="[THT]"]
  S4 = Pushbutton [package="[THT]"]
  S5 = Pushbutton [package="[THT]"]
  S6 = Pushbutton [package="[THT]"]
  S7 = Pushbutton [package="[THT]"]
  S8 = Pushbutton [package="[THT]"]
  S9 = Pushbutton [package="[THT]"]
  LED1 = LED - 5mm [color="Red (633nm)" package="5 mm [THT]"]
  LED2 = LED - 5mm [color="Red (633nm)" package="5 mm [THT]"]
  R2 = Rotary Potentiometer (Large) [maximum_resistance=10kΩ package=THT]
  R3 = Rotary Potentiometer (Large) [maximum_resistance=10kΩ package=THT]
  R1 = Resistor [tolerance=±5% resistance=10k package=THT]
  R4 = Resistor [tolerance=±5% resistance=91 package=THT]
  R5 = Resistor [tolerance=±5% resistance=91 package=THT]
  S10 = Toggle Switch [package=THT]
  S11 = Toggle Switch [package=THT]
  JP2 = Header 6 [package=1x06_smd_straight_alt]
  C1 = Ceramic Capacitor [capacitance=100nF voltage=10V package="200 mil [THT, multilayer]"]

nets:
  N1: U1.RESET, R1.Pin_0
  N2: U1.D0_(RX), S11.L2
  N3: U1.D1_(TX), S10.L2
  N4: U1.D2, S1.Pin_3, S1.Pin_4
  N5: U1.D3_(PWM), S6.Pin_3, S6.Pin_4
  N6: U1.D4, S5.Pin_3, S5.Pin_4
  N7: U1.VCC, U1.AVCC, R2.leg2, R3.leg2, R1.Pin_1, JP2.1, JP2.3, C1.0
  N8: U1.GND, S1.Pin_1, S1.Pin_2, S2.Pin_1, S2.Pin_2, S3.Pin_1, S3.Pin_2, S4.Pin_1, S4.Pin_2, S5.Pin_1, S5.Pin_2, S6.Pin_1, S6.Pin_2, S7.Pin_1, S7.Pin_2, S8.Pin_1, S8.Pin_2, S9.Pin_1, S9.Pin_2, R2.leg1, R3.leg1, R4.Pin_0, R5.Pin_0, S10.COM, S11.L1, S11.COM, JP2.6, C1.1
  N9: U1.D5_(PWM), S2.Pin_3, S2.Pin_4
  N10: U1.D6_(PWM), S3.Pin_3, S3.Pin_4
  N11: U1.D7, S4.Pin_3, S4.Pin_4
  N12: U1.D8, LED1.cathode
  N13: U1.D9_(PWM), LED2.cathode
  N14: U1.D10_(PWM), S7.Pin_3, S7.Pin_4
  N15: U1.D11_(PWM), S8.Pin_3, S8.Pin_4
  N16: U1.D13, S9.Pin_3, S9.Pin_4
  N17: U1.A0, R3.wiper
  N18: U1.A1, R2.wiper
  N19: U1.A4, JP2.5
  N20: U1.A5, JP2.2
  N21: LED1.anode, R5.Pin_1
  N22: LED2.anode, R4.Pin_1

notes:
  Wii cable
  Red - 3.3V
  Yellow - SCL
  Green - SDA
  Black - GND

custom parts:
  Header 6: Header 6 Standard 6-pin 0.1 header. Use with straight break away headers (SKU : PRT-00116), right angle break away headers (PRT-00553), swiss pins (PRT-00743), machine pins (PRT-00117), and female headers (PRT-00115). Molex polarized connector foot print use with SKU : PRT-08094 with associated crimp pins and housings. NOTES ON THE VARIANTS LOCK and LOCK_LONGPADS... This footprint was designed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
